# Fritzing sketch Untitled Sketch (saved by Fritzing 0.9.2b)
circuit board: 9.5cm x 2.6cm
breadboards: 1

parts:
  Part1 = Arduino Nano (Rev3.0)
  J1 = female pin header, 10 pins [form="♀ (female)"]

nets:
  N1: Part1.GND, J1.pin2
  N2: Part1.5V, J1.pin1
  N3: Part1.A5, J1.pin3
  N4: Part1.A4, J1.pin4
